# Fritzing sketch 01_led (saved by Fritzing 0.9.1b)
breadboards: 1

parts:
  R2 = Resistor [tolerance=±5% resistance=220 package=THT]
  LED1 = LED - 5mm [color="Red (633nm)" package="5 mm [THT]"]
  Raspberry_Pi1 = Raspberry Pi B+

nets:
  N1: R2.Pin_0, Raspberry_Pi1.3v3
  N2: R2.Pin_1, LED1.anode
  N3: LED1.cathode, Raspberry_Pi1.GPIO17
