# Fritzing sketch 01_led_T_cobbler (saved by Fritzing 0.8.7b)
breadboards: 1

parts:
  T-Cobbler1 = T-Cobbler
  R1 = Resistor [package="2010 [SMD]"]
  LED1 = LED - 5mm [color="Red (633nm)" package="5 mm [THT]"]

nets:
  N1: T-Cobbler1.3V3#0, R1.Pin_1
  N2: T-Cobbler1.GPIO17, LED1.cathode
  N3: R1.Pin_0, LED1.anode

custom parts:
  T-Cobbler: T-Cobbler for RPi B+ and Rpi2 from SunFounder
