# Fritzing sketch 03_8Led (saved by Fritzing 0.9.2b)
breadboards: 1

parts:
  R2 = Resistor [tolerance=±5% resistance=220 package=THT]
  LED1 = LED - 5mm [color="Red (633nm)" package="5 mm [THT]"]
  LED2 = LED - 5mm [color="Red (633nm)" package="5 mm [THT]"]
  LED3 = LED - 5mm [color="Red (633nm)" package="5 mm [THT]"]
  LED4 = LED - 5mm [color="Red (633nm)" package="5 mm [THT]"]
  LED5 = LED - 5mm [color="Red (633nm)" package="5 mm [THT]"]
  LED6 = LED - 5mm [color="Red (633nm)" package="5 mm [THT]"]
  LED7 = LED - 5mm [color="Red (633nm)" package="5 mm [THT]"]
  LED8 = LED - 5mm [color="Red (633nm)" package="5 mm [THT]"]
  R3 = Resistor [tolerance=±5% resistance=220 package=THT]
  R4 = Resistor [tolerance=±5% resistance=220 package=THT]
  R5 = Resistor [tolerance=±5% resistance=220 package=THT]
  R6 = Resistor [tolerance=±5% resistance=220 package=THT]
  R8 = Resistor [tolerance=±5% resistance=220 package=THT]
  Raspberry_Pi1 = Raspberry Pi B+
  R7 = Resistor [tolerance=±5% resistance=220 package="2010 [SMD]"]
  R9 = Resistor [tolerance=±5% resistance=220 package="2010 [SMD]"]

nets:
  N1: R2.Pin_0, R3.Pin_1, R4.Pin_1, R5.Pin_1, R6.Pin_1, R8.Pin_1, Raspberry_Pi1.3v3, R7.Pin_1, R9.Pin_1
  N2: R2.Pin_1, LED1.anode
  N3: LED1.cathode, Raspberry_Pi1.GPIO17
  N4: LED2.cathode, Raspberry_Pi1.GPIO18
  N5: LED2.anode, R3.Pin_0
  N6: LED3.cathode, Raspberry_Pi1.GPIO27
  N7: LED3.anode, R4.Pin_0
  N8: LED4.cathode, Raspberry_Pi1.GPIO22
  N9: LED4.anode, R6.Pin_0
  N10: LED5.cathode, Raspberry_Pi1.GPIO25
  N11: LED5.anode, R9.Pin_0
  N12: LED6.cathode, Raspberry_Pi1.GPIO4
  N13: LED6.anode, R8.Pin_0
  N14: LED7.cathode, Raspberry_Pi1.GPIO23
  N15: LED7.anode, R5.Pin_0
  N16: LED8.cathode, Raspberry_Pi1.GPIO24
  N17: LED8.anode, R7.Pin_0
