# Fritzing sketch 03_8Led_T_cobbler (saved by Fritzing 0.8.7b)
breadboards: 1

parts:
  T-Cobbler1 = T-Cobbler
  R1 = Resistor [tolerance=±5% resistance=220 package=THT]
  R2 = Resistor [tolerance=±5% resistance=220 package=THT]
  R3 = Resistor [tolerance=±5% resistance=220 package=THT]
  R4 = Resistor [tolerance=±5% resistance=220 package=THT]
  R5 = Resistor [tolerance=±5% resistance=220 package=THT]
  R6 = Resistor [tolerance=±5% resistance=220 package=THT]
  R7 = Resistor [tolerance=±5% resistance=220 package=THT]
  R8 = Resistor [tolerance=±5% resistance=220 package=THT]
  LED1 = LED - 5mm [color="Red (633nm)" package="5 mm [THT]"]
  LED2 = LED - 5mm [color="Red (633nm)" package="5 mm [THT]"]
  LED3 = LED - 5mm [color="Green (565nm)" package="5 mm [THT]"]
  LED4 = LED - 5mm [color="Green (565nm)" package="5 mm [THT]"]
  LED5 = LED - 5mm [color="Yellow (595nm)" package="5 mm [THT]"]
  LED6 = LED - 5mm [color="Yellow (595nm)" package="5 mm [THT]"]
  LED7 = LED - 5mm [color="Red (633nm)" package="5 mm [THT]"]
  LED8 = LED - 5mm [color="Red (633nm)" package="5 mm [THT]"]

nets:
  N1: T-Cobbler1.3V3#0, R1.Pin_1, R2.Pin_1, R3.Pin_1, R4.Pin_1, R5.Pin_1, R6.Pin_1, R7.Pin_1, R8.Pin_1
  N2: T-Cobbler1.GPIO4, LED8.cathode
  N3: T-Cobbler1.GPIO17, LED1.cathode
  N4: T-Cobbler1.GPIO27, LED3.cathode
  N5: T-Cobbler1.GPIO22, LED4.cathode
  N6: T-Cobbler1.GPIO18, LED2.cathode
  N7: T-Cobbler1.GPIO23, LED5.cathode
  N8: T-Cobbler1.GPIO24, LED6.cathode
  N9: T-Cobbler1.GPIO25, LED7.cathode
  N10: R1.Pin_0, LED1.anode
  N11: R2.Pin_0, LED2.anode
  N12: R3.Pin_0, LED3.anode
  N13: R4.Pin_0, LED8.anode
  N14: R5.Pin_0, LED4.anode
  N15: R6.Pin_0, LED5.anode
  N16: R7.Pin_0, LED6.anode
  N17: R8.Pin_0, LED7.anode

custom parts:
  T-Cobbler: T-Cobbler for RPi B+ and Rpi2 from SunFounder
