# Fritzing sketch 05_RGB (saved by Fritzing 0.9.1b)
breadboards: 1

parts:
  R2 = Resistor [tolerance=±5% resistance=220 package=THT]
  R3 = Resistor [tolerance=±5% resistance=220 package=THT]
  R4 = Resistor [tolerance=±5% resistance=220 package=THT]
  LED1 = RGB LED (com. cathode, rgb) [package="5 mm [THT]"]
  Raspberry_Pi1 = Raspberry Pi B+

nets:
  N1: R2.Pin_0, Raspberry_Pi1.GPIO17
  N2: R2.Pin_1, LED1.red_anode
  N3: R3.Pin_0, Raspberry_Pi1.GPIO18
  N4: R3.Pin_1, LED1.green_anode
  N5: R4.Pin_0, Raspberry_Pi1.GPIO27
  N6: R4.Pin_1, LED1.blue_anode
  N7: LED1.common_cathode, Raspberry_Pi1.GND
