# Fritzing sketch 06_Beep (saved by Fritzing 0.9.1b)
breadboards: 1

parts:
  R2 = Resistor [tolerance=±5% resistance=220 package=THT]
  J1 = Piezo Speaker
  Q1 = PNP-Transistor [package="SOT-23 [SMD]"]
  Raspberry_Pi1 = Raspberry Pi B+

nets:
  N1: R2.Pin_0, Q1.0
  N2: R2.Pin_1, Raspberry_Pi1.GPIO17
  N3: J1.pin1, Q1.2
  N4: J1.pin2, Raspberry_Pi1.5V
  N5: Q1.1, Raspberry_Pi1.GND
