# Fritzing sketch 09_Timer555 (saved by Fritzing 0.9.1b)
breadboards: 1

parts:
  U1 = 555 Timer [package="DIP8 [THT]"]
  C1 = Capacitor [package=cap-pth-small2]
  C2 = Capacitor [package=cap-pth-small2]
  Raspberry_Pi1 = Raspberry Pi B+
  R5 = Resistor [tolerance=±5% resistance=10k package=THT]
  R6 = Resistor [tolerance=±5% resistance=10k package=THT]
  R7 = Resistor [tolerance=±5% resistance=1k package=THT]

nets:
  N1: U1.Ground, C1.2, C2.1, Raspberry_Pi1.GND
  N2: U1.Trigger, U1.Threshold, C1.1, C2.2, R5.Pin_1
  N3: U1.Output, R7.Pin_1
  N4: U1.Reset, U1.Vcc_Supply_Voltage, Raspberry_Pi1.5V, R6.Pin_0
  N5: U1.Discharge, R5.Pin_0, R6.Pin_1
  N6: Raspberry_Pi1.GPIO17, R7.Pin_0
