# Fritzing sketch 10_74hc595_LED (saved by Fritzing 0.9.1b)
breadboards: 1

parts:
  U1 = 74HC595 SMD [package="SO16 [SMD]"]
  LED1 = smd LED [color="Red (633nm)" package="1206 [SMD]"]
  LED2 = smd LED [color="Red (633nm)" package="1206 [SMD]"]
  LED3 = smd LED [color="Red (633nm)" package="1206 [SMD]"]
  LED4 = smd LED [color="Red (633nm)" package="1206 [SMD]"]
  LED5 = smd LED [color="Red (633nm)" package="1206 [SMD]"]
  LED6 = smd LED [color="Red (633nm)" package="1206 [SMD]"]
  LED7 = smd LED [color="Red (633nm)" package="1206 [SMD]"]
  LED8 = smd LED [color="Red (633nm)" package="1206 [SMD]"]
  Raspberry_Pi1 = Raspberry Pi B+
  R1 = Resistor [tolerance=±5% resistance=220 package="1206 [SMD]"]
  R2 = Resistor [tolerance=±5% resistance=220 package="1206 [SMD]"]
  R3 = Resistor [tolerance=±5% resistance=220 package="1206 [SMD]"]
  R4 = Resistor [tolerance=±5% resistance=220 package="1206 [SMD]"]
  R5 = Resistor [tolerance=±5% resistance=220 package="1206 [SMD]"]
  R6 = Resistor [tolerance=±5% resistance=220 package="1206 [SMD]"]
  R7 = Resistor [tolerance=±5% resistance=220 package="1206 [SMD]"]
  R8 = Resistor [tolerance=±5% resistance=220 package="1206 [SMD]"]

nets:
  N1: U1.Q1, R2.Pin_1
  N2: U1.Q2, R3.Pin_1
  N3: U1.Q3, R4.Pin_1
  N4: U1.Q4, R5.Pin_1
  N5: U1.Q5, R6.Pin_1
  N6: U1.Q6, R7.Pin_1
  N7: U1.Q7, R8.Pin_1
  GND: U1.GND, U1.OE, LED1.cathode, LED2.cathode, LED3.cathode, LED4.cathode, LED5.cathode, LED6.cathode, LED7.cathode, LED8.cathode, Raspberry_Pi1.GND
  VCC: U1.MR, U1.VCC, Raspberry_Pi1.5V
  N8: U1.SH_CP, Raspberry_Pi1.GPIO27
  N9: U1.ST_CP, Raspberry_Pi1.GPIO18
  N10: U1.DS, Raspberry_Pi1.GPIO17
  N11: U1.Q0, R1.Pin_1
  N12: LED1.anode, R8.Pin_0
  N13: LED2.anode, R7.Pin_0
  N14: LED3.anode, R6.Pin_0
  N15: LED4.anode, R5.Pin_0
  N16: LED5.anode, R3.Pin_0
  N17: LED6.anode, R2.Pin_0
  N18: LED7.anode, R1.Pin_0
  N19: LED8.anode, R4.Pin_0
