# Fritzing sketch 11_2_dict2 (saved by Fritzing 0.9.1b)
breadboards: 1

parts:
  U1 = 74HC595 SMD [package="SO16 [SMD]"]
  R6 = Resistor [tolerance=±5% resistance=220 package=THT]
  DI1 = 7-Segment LED Display [package=THT]
  Raspberry_Pi1 = Raspberry Pi B+
  S1 = Pushbutton [package="[THT]"]

nets:
  N1: U1.Q1, DI1.cathodeB
  N2: U1.Q2, DI1.cathodeC
  N3: U1.Q3, DI1.cathodeD
  N4: U1.Q4, DI1.cathodeE
  N5: U1.Q5, DI1.cathodeF
  N6: U1.Q6, DI1.cathodeG
  N7: U1.Q7, DI1.cathodeDP
  GND: U1.GND, U1.OE, R6.Pin_1, Raspberry_Pi1.GND, S1.Pin_1
  VCC: U1.MR, U1.VCC, Raspberry_Pi1.5V
  N8: U1.SH_CP, Raspberry_Pi1.GPIO27
  N9: U1.ST_CP, Raspberry_Pi1.GPIO18
  N10: U1.DS, Raspberry_Pi1.GPIO17
  N11: U1.Q0, DI1.cathodeA
  N12: R6.Pin_0, DI1.commAnode#2
