# Fritzing sketch 12_Dot-matrix Display (saved by Fritzing 0.9.2b)
breadboards: 1

parts:
  module1 = 788BS Dot matix
  Raspberry_Pi1 = Raspberry Pi B+
  U1 = 74HC595 [package="DIP16 [THT]"]
  U2 = 74HC595 [package="DIP16 [THT]"]

nets:
  N1: module1.P1, U1.Q4
  N2: module1.P2, U1.Q6
  N3: module1.P3, U2.Q1
  N4: module1.P4, U2.Q2
  N5: module1.P5, U1.Q7
  N6: module1.P6, U2.Q4
  N7: module1.P7, U1.Q5
  N8: module1.P8, U1.Q2
  N9: module1.P9, U1.Q0
  N10: module1.P10, U2.Q3
  N11: module1.P11, U2.Q5
  N12: module1.P12, U1.Q3
  N13: module1.P13, U2.Q0
  N14: module1.P14, U1.Q1
  N15: module1.P15, U2.Q6
  N16: module1.P16, U2.Q7
  N17: Raspberry_Pi1.GPIO17, U1.DS
  N18: Raspberry_Pi1.GPIO27, U1.SH_CP, U2.SH_CP
  N19: Raspberry_Pi1.GPIO18, U1.ST_CP, U2.ST_CP
  GND: Raspberry_Pi1.GND, U1.GND, U1.OE, U2.GND, U2.OE
  VCC: Raspberry_Pi1.5V, U1.MR, U1.VCC, U2.MR, U2.VCC
  N20: U1.Q7', U2.DS

custom parts:
  788BS Dot matix: 788BS 8x8 dot matix from SunFounder
