# Fritzing sketch 13_LCD1602 (saved by Fritzing 0.8.7b)
breadboards: 1

parts:
  LCD1 = LCD screen
  U1 = POT [package=alps_pot]
  Raspberry_Pi_B_rev1 = Raspberry Pi 2

nets:
  VSS: LCD1.VSS, LCD1.R/W, LCD1.LED-, U1.E, Raspberry_Pi_B_rev1.GND
  VDD: LCD1.VDD, U1.A, Raspberry_Pi_B_rev1.5V
  N1: LCD1.V0, U1.S
  N2: LCD1.RS, Raspberry_Pi_B_rev1.GIPO27
  N3: LCD1.E, Raspberry_Pi_B_rev1.GIPO22
  N4: LCD1.DB4, Raspberry_Pi_B_rev1.GIPO25
  N5: LCD1.DB5, Raspberry_Pi_B_rev1.GIPO24
  N6: LCD1.DB6, Raspberry_Pi_B_rev1.GIPO23
  N7: LCD1.DB7, Raspberry_Pi_B_rev1.GIPO18
  N8: LCD1.LED+, Raspberry_Pi_B_rev1.3v3

custom parts:
  Raspberry Pi 2: The RPi2, a faster version of the awesome Raspberry Pi B+ ARM Board with 40 pin gipo. Ready for special Raspberry Pi B+ and RPi2 Hat (Hardware attached (on) top)
