# Fritzing sketch 14_ADXL345 (saved by Fritzing 0.8.7b)
breadboards: 1

parts:
  3-axis_accelerometer1 = ADXL345 [package=THT]
  Raspberry_Pi_B_rev1 = Raspberry Pi 2

nets:
  GND: 3-axis_accelerometer1.GND, 3-axis_accelerometer1.SD0, Raspberry_Pi_B_rev1.GND
  N1: 3-axis_accelerometer1.SCL, Raspberry_Pi_B_rev1.GPIO3
  N2: 3-axis_accelerometer1.SDA, Raspberry_Pi_B_rev1.GPIO2
  3.3V: 3-axis_accelerometer1.3.3V, 3-axis_accelerometer1.VS, Raspberry_Pi_B_rev1.3v3

notes:
  ADXL345

custom parts:
  ADXL345: An ADXL345 is a small, thin, low power, 3-axis accelerometer with high resolution (13-bit) measurement at up to ±16 g. Digital output data is formatted as 16-bit two’s complement and is accessible through either an SPI (3- or 4-wire) or I2C digital interface.
  Raspberry Pi 2: The RPi2, a faster version of the awesome Raspberry Pi B+ ARM Board with 40 pin gipo. Ready for special Raspberry Pi B+ and RPi2 Hat (Hardware attached (on) top)
